# Fritzing sketch temp sensor LCD (saved by Fritzing 0.9.2b)
breadboards: 1

parts:
  LCD1 = LCD screen
  R1 = Trimmer Potentiometer [maximum_resistance=10kΩ package=THT]
  Arduino_UNO = Arduino Uno (Rev3)
  LM35 = LM35 Temperature Sensor [package="TO92 [THT]"]

nets:
  GND: LCD1.VSS, R1.leg1, Arduino_UNO.GND, LM35.GND
  N1: LCD1.V0, R1.wiper
  N2: LCD1.RS, Arduino_UNO.D12/MISO
  N3: LCD1.E, Arduino_UNO.D11_PWM/MOSI
  N4: LCD1.DB4, Arduino_UNO.D5_PWM
  N5: LCD1.DB5, Arduino_UNO.D4
  N6: LCD1.DB6, Arduino_UNO.D3_PWM
  N7: LCD1.DB7, Arduino_UNO.D2
  N8: R1.leg2, Arduino_UNO.5V, LM35.+Vs
  N9: Arduino_UNO.A0, LM35.Vout
