# Fritzing sketch prox sensor RGB (saved by Fritzing 0.9.2b)
breadboards: 1

parts:
  Part1 = SRF05 Ultrasonic Rangefinder
  Part2 = Arduino Uno (Rev3)
  LED1 = RGB LED (com. cathode, rgb) [package="5 mm [THT]"]

nets:
  VCC: Part1.VCC, Part2.5V, LED1.common_cathode
  N1: Part1.Trig, Part2.D7
  N2: Part1.Echo, Part2.D8
  GND: Part1.GND, Part2.GND
  N3: Part2.D2, LED1.green_anode
  N4: Part2.D3_PWM, LED1.blue_anode
  N5: Part2.D4, LED1.red_anode
